# Fritzing sketch IoTWeatherLogger (saved by Fritzing 0.9.2b)

parts:
  DHT1 = DHT11 Humitidy and Temperature Sensor
  Part2 = GY-86
  Part3 = ESPDuino

nets:
  N1: DHT1.NULL, Part3.5V#87
  GND: DHT1.GND, Part2.GND, Part3.GND
  N2: Part2.VCC_IN, Part3.5V#84
  N3: Part2.SCL, Part3.SCL
  N4: Part2.SDA, Part3.SDA

custom parts:
  DHT11 Humitidy and Temperature Sensor: DHT11 Humidity and Temperature Sensor
  ESPDuino: ESPDuino=WiFi + UNO R3 Compatible with Arduino Development Board from ESP8266 ESP-13 DIY RC Toy Remote Control Introduction ESPduino is developed by Doit company based on the ESP8266 ESP-13, which can be compatible with Arduino UNO R3 developmen board. By using the ESP8266 WiFi and MCU, ESPduino supports WiFi. Compared to the traditional Arduino UNO development baord, users don't have to buy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
